// Logisim project riscv_modules.circ as structural Verilog: 20 circuits, main circuit ALU
module ALU (
  input  [31:0] A,
  input  [31:0] B,
  input  [3:0] ALUctl,
  output [31:0] Y,
  output Zero
);

  wire comparator_1_lt, comparator_2_lt;
  wire [31:0] bit_extender_1_out, r_addsub, r_and, r_or, r_sll, r_slt, r_sltu, r_sra, r_srl, r_xor, xor_1_out;

  assign bit_extender_1_out = {{31{ALUctl[0]}}, ALUctl[0]};  // Bit_Extender bit_extender_1
  assign r_and = A & B;  // AND_Gate and_1, 32 bits wide
  assign r_or = A | B;  // OR_Gate or_1, 32 bits wide
  Shifter #(.width(32)) shifter_1 (.in(A), .\dist (B[4:0]), .out(r_sll));
  Shifter #(.shift("lr"), .width(32)) shifter_2 (.in(A), .\dist (B[4:0]), .out(r_srl));
  Shifter #(.shift("ar"), .width(32)) shifter_3 (.in(A), .\dist (B[4:0]), .out(r_sra));
  Comparator #(.width(32)) comparator_1 (.a(A), .b(B), .lt(comparator_1_lt));  // open: gt, eq
  Comparator #(.mode("unsigned"), .width(32)) comparator_2 (.a(A), .b(B), .lt(comparator_2_lt));  // open: gt, eq
  assign xor_1_out = bit_extender_1_out ^ B;  // XOR_Gate xor_1, 32 bits wide
  assign r_xor = A ^ B;  // XOR_Gate xor_2, 32 bits wide
  Adder #(.width(32)) adder_1 (.a(A), .b(xor_1_out), .out(r_addsub), .cin(ALUctl[0]));  // open: cout
  assign r_slt = {{31{1'b0}}, comparator_1_lt};  // Bit_Extender bit_extender_2
  assign r_sltu = {{31{1'b0}}, comparator_2_lt};  // Bit_Extender bit_extender_3
  Multiplexer #(.select(4), .width(32)) multiplexer_1 (
    .in0(r_addsub), .in1(r_addsub), .in2(r_and), .in3(r_or), .in4(r_xor), .in5(r_slt), .in6(r_sltu),
    .in7(r_sll), .in8(r_srl), .in9(r_sra), .in10(B), .in11({32{1'b0}}), .in12({32{1'b0}}), .in13({32{1'b0}}),
    .in14({32{1'b0}}), .in15({32{1'b0}}), .out(Y), .sel(ALUctl));
  Comparator #(.width(32)) comparator_3 (.a(Y), .b({32{1'b0}}), .eq(Zero));  // open: gt, lt

  // Other names for the same wires on the sheet: ctl[3:0] = ALUctl; Yint[31:0] = Y
endmodule

module RegFile (
  input  [4:0] rs1,
  input  [4:0] rs2,
  input  [4:0] rd,
  input  [31:0] WD,
  input  RegWrite,
  input  clk,
  input  Reset,
  output [31:0] RD1,
  output [31:0] RD2
);

  wire we1, we2, we3, we4, we5, we6, we7, we8, we9, we10, we11, we12, we13, we14, we15, we16, we17, we18,
       we19, we20, we21, we22, we23, we24, we25, we26, we27, we28, we29, we30, we31;
  wire [31:0] q1, q2, q3, q4, q5, q6, q7, q8, q9, q10, q11, q12, q13, q14, q15, q16, q17, q18, q19, q20, q21,
       q22, q23, q24, q25, q26, q27, q28, q29, q30, q31;

  Register #(.width(32)) x1 (.D(WD), .en(we1), .clk(clk), .Q(q1), .clr(Reset));
  Register #(.width(32)) x9 (.D(WD), .en(we9), .clk(clk), .Q(q9), .clr(Reset));
  Register #(.width(32)) x17 (.D(WD), .en(we17), .clk(clk), .Q(q17), .clr(Reset));
  Register #(.width(32)) x25 (.D(WD), .en(we25), .clk(clk), .Q(q25), .clr(Reset));
  Decoder #(.select(5)) decoder_1 (
    .out1(we1), .out2(we2), .out3(we3), .out4(we4), .out5(we5), .out6(we6), .out7(we7), .out8(we8),
    .out9(we9), .out10(we10), .out11(we11), .out12(we12), .out13(we13), .out14(we14), .out15(we15),
    .out16(we16), .out17(we17), .out18(we18), .out19(we19), .out20(we20), .out21(we21), .out22(we22),
    .out23(we23), .out24(we24), .out25(we25), .out26(we26), .out27(we27), .out28(we28), .out29(we29),
    .out30(we30), .out31(we31), .sel(rd), .en(RegWrite));  // open: out0
  Register #(.width(32)) x2 (.D(WD), .en(we2), .clk(clk), .Q(q2), .clr(Reset));
  Register #(.width(32)) x10 (.D(WD), .en(we10), .clk(clk), .Q(q10), .clr(Reset));
  Register #(.width(32)) x18 (.D(WD), .en(we18), .clk(clk), .Q(q18), .clr(Reset));
  Register #(.width(32)) x26 (.D(WD), .en(we26), .clk(clk), .Q(q26), .clr(Reset));
  Register #(.width(32)) x3 (.D(WD), .en(we3), .clk(clk), .Q(q3), .clr(Reset));
  Register #(.width(32)) x11 (.D(WD), .en(we11), .clk(clk), .Q(q11), .clr(Reset));
  Register #(.width(32)) x19 (.D(WD), .en(we19), .clk(clk), .Q(q19), .clr(Reset));
  Register #(.width(32)) x27 (.D(WD), .en(we27), .clk(clk), .Q(q27), .clr(Reset));
  Register #(.width(32)) x4 (.D(WD), .en(we4), .clk(clk), .Q(q4), .clr(Reset));
  Register #(.width(32)) x12 (.D(WD), .en(we12), .clk(clk), .Q(q12), .clr(Reset));
  Register #(.width(32)) x20 (.D(WD), .en(we20), .clk(clk), .Q(q20), .clr(Reset));
  Register #(.width(32)) x28 (.D(WD), .en(we28), .clk(clk), .Q(q28), .clr(Reset));
  Register #(.width(32)) x5 (.D(WD), .en(we5), .clk(clk), .Q(q5), .clr(Reset));
  Register #(.width(32)) x13 (.D(WD), .en(we13), .clk(clk), .Q(q13), .clr(Reset));
  Register #(.width(32)) x21 (.D(WD), .en(we21), .clk(clk), .Q(q21), .clr(Reset));
  Register #(.width(32)) x29 (.D(WD), .en(we29), .clk(clk), .Q(q29), .clr(Reset));
  Register #(.width(32)) x6 (.D(WD), .en(we6), .clk(clk), .Q(q6), .clr(Reset));
  Register #(.width(32)) x14 (.D(WD), .en(we14), .clk(clk), .Q(q14), .clr(Reset));
  Register #(.width(32)) x22 (.D(WD), .en(we22), .clk(clk), .Q(q22), .clr(Reset));
  Register #(.width(32)) x30 (.D(WD), .en(we30), .clk(clk), .Q(q30), .clr(Reset));
  Multiplexer #(.select(5), .width(32)) multiplexer_1 (
    .in0({32{1'b0}}), .in1(q1), .in2(q2), .in3(q3), .in4(q4), .in5(q5), .in6(q6), .in7(q7), .in8(q8),
    .in9(q9), .in10(q10), .in11(q11), .in12(q12), .in13(q13), .in14(q14), .in15(q15), .in16(q16), .in17(q17),
    .in18(q18), .in19(q19), .in20(q20), .in21(q21), .in22(q22), .in23(q23), .in24(q24), .in25(q25),
    .in26(q26), .in27(q27), .in28(q28), .in29(q29), .in30(q30), .in31(q31), .out(RD1), .sel(rs1));
  Register #(.width(32)) x7 (.D(WD), .en(we7), .clk(clk), .Q(q7), .clr(Reset));
  Register #(.width(32)) x15 (.D(WD), .en(we15), .clk(clk), .Q(q15), .clr(Reset));
  Register #(.width(32)) x23 (.D(WD), .en(we23), .clk(clk), .Q(q23), .clr(Reset));
  Register #(.width(32)) x31 (.D(WD), .en(we31), .clk(clk), .Q(q31), .clr(Reset));
  Register #(.width(32)) x8 (.D(WD), .en(we8), .clk(clk), .Q(q8), .clr(Reset));
  Register #(.width(32)) x16 (.D(WD), .en(we16), .clk(clk), .Q(q16), .clr(Reset));
  Register #(.width(32)) x24 (.D(WD), .en(we24), .clk(clk), .Q(q24), .clr(Reset));
  Multiplexer #(.select(5), .width(32)) multiplexer_2 (
    .in0({32{1'b0}}), .in1(q1), .in2(q2), .in3(q3), .in4(q4), .in5(q5), .in6(q6), .in7(q7), .in8(q8),
    .in9(q9), .in10(q10), .in11(q11), .in12(q12), .in13(q13), .in14(q14), .in15(q15), .in16(q16), .in17(q17),
    .in18(q18), .in19(q19), .in20(q20), .in21(q21), .in22(q22), .in23(q23), .in24(q24), .in25(q25),
    .in26(q26), .in27(q27), .in28(q28), .in29(q29), .in30(q30), .in31(q31), .out(RD2), .sel(rs2));
endmodule

module ImmGen (
  input  [31:0] Instr,
  input  [2:0] ImmSel,
  output [31:0] Imm
);

  wire [31:0] imm_B, imm_I, imm_J, imm_S, imm_U;

  assign imm_U = Instr & 32'hfffff000;  // AND_Gate and_1, 32 bits wide
  assign imm_I = {{20{Instr[31]}}, Instr[31:20]};  // Bit_Extender bit_extender_1
  assign imm_S = {{20{Instr[31]}}, {Instr[31:25], Instr[11:7]}};  // Bit_Extender bit_extender_2
  assign imm_B = {{19{Instr[31]}}, {Instr[31], Instr[7], Instr[30:25], Instr[11:8], 1'b0}};  // Bit_Extender bit_extender_3
  assign imm_J = {{11{Instr[31]}}, {Instr[31], Instr[19:12], Instr[20], Instr[30:21], 1'b0}};  // Bit_Extender bit_extender_4
  Multiplexer #(.select(3), .width(32)) multiplexer_1 (
    .in0(imm_I), .in1(imm_S), .in2(imm_B), .in3(imm_U), .in4(imm_J), .in5({32{1'b0}}), .in6({32{1'b0}}),
    .in7({32{1'b0}}), .out(Imm), .sel(ImmSel));

  // Other names for the same wires on the sheet: ins[31:0] = Instr
endmodule

module BranchCmp (
  input  [31:0] A,
  input  [31:0] B,
  input  [2:0] funct3,
  output Eq,
  output Lt,
  output Taken,
  output Ltu
);

  wire not_1_out, not_2_out, not_3_out;

  Comparator #(.width(32)) comparator_1 (.a(A), .b(B), .eq(Eq), .lt(Lt));  // open: gt
  Comparator #(.mode("unsigned"), .width(32)) comparator_2 (.a(A), .b(B), .lt(Ltu));  // open: gt, eq
  not not_1 (not_1_out, Eq);
  not not_2 (not_2_out, Lt);
  not not_3 (not_3_out, Ltu);
  Multiplexer #(.select(3)) multiplexer_1 (
    .in0(Eq), .in1(not_1_out), .in2(1'b0), .in3(1'b0), .in4(Lt), .in5(not_2_out), .in6(Ltu), .in7(not_3_out),
    .out(Taken), .sel(funct3));
endmodule

module PCUnit (
  input  [31:0] PCnext,
  input  EN,
  input  clk,
  input  Reset,
  output [31:0] PC,
  output [31:0] PC4
);

  Register #(.width(32)) register_1 (.D(PCnext), .en(EN), .clk(clk), .Q(PC), .clr(Reset));
  Adder #(.width(32)) adder_1 (.a(PC), .b(32'h4), .out(PC4));  // open: cin, cout
endmodule

module Control (
  input  [31:0] Instr,
  output [3:0] ALUctl,
  output [1:0] MemToReg,
  output MemWrite,
  output MemRead,
  output ALUSrc,
  output RegWrite,
  output Branch,
  output Jump,
  output Jalr,
  output [2:0] ImmSel
);

  wire [1:0] ALUOp;

  ROM #(.addrWidth(7), .dataWidth(14)) CTRL_ROM (
    .addr(Instr[6:0]),
    .data({ImmSel, ALUOp, Jalr, Jump, Branch, MemToReg, MemWrite, MemRead, ALUSrc, RegWrite}));
  ROM #(.addrWidth(6), .dataWidth(4)) ALU_ROM (.addr({ALUOp, Instr[14:12], Instr[30]}), .data(ALUctl));

  // Other names for the same wires on the sheet: b30 = Instr[30]; funct3[2:0] = Instr[14:12];
  //   opcode[6:0] = Instr[6:0]

  // Notes on the sheet:
  //   contents of CTRL_ROM (hex, n*v repeats v):
  //   0 0 0 17 15*0 603 15*0 80a 15*0 401 0 0 0 1a03 43*0 1040 0 0 0 123 7*0 20a1
  //   contents of ALU_ROM (hex, n*v repeats v):
  //   16*0 16*a 0 1 7 7 5 5 6 6 4 4 8 9 3 3 2 2 0 0 7 7 5 5 6 6 4 4 8 9 3 3 2 2
endmodule

module IF_ID (
  input  EN,
  input  [31:0] PC_in,
  input  Flush,
  input  clk,
  input  Reset,
  input  [31:0] PC4_in,
  input  [31:0] Instr_in,
  output [31:0] PC_out,
  output [31:0] PC4_out,
  output [31:0] Instr_out
);

  wire ld;
  wire [31:0] multiplexer_1_out;

  or or_1 (ld, EN, Flush);
  Multiplexer #(.width(32)) multiplexer_1 (.in0(Instr_in), .in1({32{1'b0}}), .out(multiplexer_1_out), .sel(Flush));
  Register #(.width(32)) rPC (.D(PC_in), .en(ld), .clk(clk), .Q(PC_out), .clr(Reset));
  Register #(.width(32)) rPC4 (.D(PC4_in), .en(ld), .clk(clk), .Q(PC4_out), .clr(Reset));
  Register #(.width(32)) rInstr (.D(multiplexer_1_out), .en(ld), .clk(clk), .Q(Instr_out), .clr(Reset));
endmodule

module MEM_WB (
  input  EN,
  input  [31:0] PC_in,
  input  Flush,
  input  clk,
  input  Reset,
  input  [31:0] Result_in,
  input  [31:0] Instr_in,
  input  [31:0] RData_in,
  input  [4:0] rd_in,
  input  RegWrite_in,
  input  [1:0] MemToReg_in,
  output [31:0] PC_out,
  output [31:0] Result_out,
  output [31:0] Instr_out,
  output [31:0] RData_out,
  output [4:0] rd_out,
  output RegWrite_out,
  output [1:0] MemToReg_out
);

  wire ld, multiplexer_2_out;
  wire [1:0] multiplexer_3_out;
  wire [31:0] multiplexer_1_out;

  or or_1 (ld, EN, Flush);
  Multiplexer #(.width(32)) multiplexer_1 (.in0(Instr_in), .in1({32{1'b0}}), .out(multiplexer_1_out), .sel(Flush));
  Multiplexer multiplexer_2 (.in0(RegWrite_in), .in1(1'b0), .out(multiplexer_2_out), .sel(Flush));
  Multiplexer #(.width(2)) multiplexer_3 (.in0(MemToReg_in), .in1(2'b00), .out(multiplexer_3_out), .sel(Flush));
  Register #(.width(32)) rPC (.D(PC_in), .en(ld), .clk(clk), .Q(PC_out), .clr(Reset));
  Register #(.width(32)) rResult (.D(Result_in), .en(ld), .clk(clk), .Q(Result_out), .clr(Reset));
  Register #(.width(32)) rInstr (.D(multiplexer_1_out), .en(ld), .clk(clk), .Q(Instr_out), .clr(Reset));
  Register #(.width(32)) rRData (.D(RData_in), .en(ld), .clk(clk), .Q(RData_out), .clr(Reset));
  Register #(.width(5)) rRd (.D(rd_in), .en(ld), .clk(clk), .Q(rd_out), .clr(Reset));
  Register #(.width(1)) rRegWrite (.D(multiplexer_2_out), .en(ld), .clk(clk), .Q(RegWrite_out), .clr(Reset));
  Register #(.width(2)) rMemToReg (.D(multiplexer_3_out), .en(ld), .clk(clk), .Q(MemToReg_out), .clr(Reset));
endmodule

module EX_MEM (
  input  EN,
  input  [31:0] PC_in,
  input  Flush,
  input  clk,
  input  Reset,
  input  [31:0] Result_in,
  input  [31:0] Instr_in,
  input  [31:0] WData_in,
  input  [4:0] rd_in,
  input  RegWrite_in,
  input  [1:0] MemToReg_in,
  input  MemRead_in,
  input  MemWrite_in,
  output [31:0] PC_out,
  output [31:0] Result_out,
  output [31:0] Instr_out,
  output [31:0] WData_out,
  output [4:0] rd_out,
  output RegWrite_out,
  output [1:0] MemToReg_out,
  output MemRead_out,
  output MemWrite_out
);

  wire ld, multiplexer_2_out, multiplexer_4_out, multiplexer_5_out;
  wire [1:0] multiplexer_3_out;
  wire [31:0] multiplexer_1_out;

  or or_1 (ld, EN, Flush);
  Multiplexer #(.width(32)) multiplexer_1 (.in0(Instr_in), .in1({32{1'b0}}), .out(multiplexer_1_out), .sel(Flush));
  Multiplexer multiplexer_2 (.in0(RegWrite_in), .in1(1'b0), .out(multiplexer_2_out), .sel(Flush));
  Multiplexer #(.width(2)) multiplexer_3 (.in0(MemToReg_in), .in1(2'b00), .out(multiplexer_3_out), .sel(Flush));
  Multiplexer multiplexer_4 (.in0(MemRead_in), .in1(1'b0), .out(multiplexer_4_out), .sel(Flush));
  Multiplexer multiplexer_5 (.in0(MemWrite_in), .in1(1'b0), .out(multiplexer_5_out), .sel(Flush));
  Register #(.width(32)) rPC (.D(PC_in), .en(ld), .clk(clk), .Q(PC_out), .clr(Reset));
  Register #(.width(32)) rResult (.D(Result_in), .en(ld), .clk(clk), .Q(Result_out), .clr(Reset));
  Register #(.width(32)) rInstr (.D(multiplexer_1_out), .en(ld), .clk(clk), .Q(Instr_out), .clr(Reset));
  Register #(.width(32)) rWData (.D(WData_in), .en(ld), .clk(clk), .Q(WData_out), .clr(Reset));
  Register #(.width(5)) rRd (.D(rd_in), .en(ld), .clk(clk), .Q(rd_out), .clr(Reset));
  Register #(.width(1)) rRegWrite (.D(multiplexer_2_out), .en(ld), .clk(clk), .Q(RegWrite_out), .clr(Reset));
  Register #(.width(2)) rMemToReg (.D(multiplexer_3_out), .en(ld), .clk(clk), .Q(MemToReg_out), .clr(Reset));
  Register #(.width(1)) rMemRead (.D(multiplexer_4_out), .en(ld), .clk(clk), .Q(MemRead_out), .clr(Reset));
  Register #(.width(1)) rMemWrite (.D(multiplexer_5_out), .en(ld), .clk(clk), .Q(MemWrite_out), .clr(Reset));
endmodule

module ID_EX (
  input  [31:0] PC_in,
  input  EN,
  input  Flush,
  input  clk,
  input  [31:0] PC4_in,
  input  Reset,
  input  [31:0] RD1_in,
  input  RegWrite_in,
  input  ALUSrc_in,
  input  [31:0] RD2_in,
  input  MemRead_in,
  input  MemWrite_in,
  input  [1:0] MemToReg_in,
  input  [31:0] Imm_in,
  input  Branch_in,
  input  Jump_in,
  input  Jalr_in,
  input  [4:0] rs1_in,
  input  [3:0] ALUctl_in,
  input  [4:0] rs2_in,
  input  [4:0] rd_in,
  input  [2:0] f3_in,
  input  [31:0] Instr_in,
  output [31:0] PC_out,
  output [31:0] PC4_out,
  output [31:0] RD1_out,
  output RegWrite_out,
  output ALUSrc_out,
  output [31:0] RD2_out,
  output MemRead_out,
  output MemWrite_out,
  output [1:0] MemToReg_out,
  output [31:0] Imm_out,
  output Branch_out,
  output Jump_out,
  output Jalr_out,
  output [4:0] rs1_out,
  output [3:0] ALUctl_out,
  output [4:0] rs2_out,
  output [4:0] rd_out,
  output [2:0] f3_out,
  output [31:0] Instr_out
);

  wire ld;
  wire [12:0] multiplexer_2_out;
  wire [31:0] multiplexer_1_out;

  or or_1 (ld, EN, Flush);
  Multiplexer #(.width(32)) multiplexer_1 (.in0(Instr_in), .in1({32{1'b0}}), .out(multiplexer_1_out), .sel(Flush));
  Multiplexer #(.width(13)) multiplexer_2 (
    .in0({ALUctl_in, Jalr_in, Jump_in, Branch_in, MemToReg_in, MemWrite_in, MemRead_in, ALUSrc_in, RegWrite_in}),
    .in1({13{1'b0}}), .out(multiplexer_2_out), .sel(Flush));
  Register #(.width(32)) rPC (.D(PC_in), .en(ld), .clk(clk), .Q(PC_out), .clr(Reset));
  Register #(.width(32)) rPC4 (.D(PC4_in), .en(ld), .clk(clk), .Q(PC4_out), .clr(Reset));
  Register #(.width(32)) rRD1 (.D(RD1_in), .en(ld), .clk(clk), .Q(RD1_out), .clr(Reset));
  Register #(.width(32)) rRD2 (.D(RD2_in), .en(ld), .clk(clk), .Q(RD2_out), .clr(Reset));
  Register #(.width(32)) rImm (.D(Imm_in), .en(ld), .clk(clk), .Q(Imm_out), .clr(Reset));
  Register #(.width(5)) rRs1 (.D(rs1_in), .en(ld), .clk(clk), .Q(rs1_out), .clr(Reset));
  Register #(.width(5)) rRs2 (.D(rs2_in), .en(ld), .clk(clk), .Q(rs2_out), .clr(Reset));
  Register #(.width(5)) rRd (.D(rd_in), .en(ld), .clk(clk), .Q(rd_out), .clr(Reset));
  Register #(.width(3)) rF3 (.D(f3_in), .en(ld), .clk(clk), .Q(f3_out), .clr(Reset));
  Register #(.width(32)) rInstr (.D(multiplexer_1_out), .en(ld), .clk(clk), .Q(Instr_out), .clr(Reset));
  Register #(.width(13)) rCtrl (
    .D(multiplexer_2_out), .en(ld), .clk(clk),
    .Q({ALUctl_out, Jalr_out, Jump_out, Branch_out, MemToReg_out, MemWrite_out, MemRead_out, ALUSrc_out, RegWrite_out}),
    .clr(Reset));

  // Other names for the same wires on the sheet: ctrl_in[12:0] = {ALUctl_in, Jalr_in, Jump_in, Branch_in, MemToReg_in, MemWrite_in, MemRead_in, ALUSrc_in, RegWrite_in};
  //   ctrl_q[12:0] = {ALUctl_out, Jalr_out, Jump_out, Branch_out, MemToReg_out, MemWrite_out, MemRead_out, ALUSrc_out, RegWrite_out}
endmodule

module ForwardUnit (
  input  [4:0] rs1_e,
  input  [4:0] rs2_e,
  input  [4:0] rd_m,
  input  RegWrite_m,
  input  [4:0] rd_w,
  input  RegWrite_w,
  output [1:0] ForwardA,
  output [1:0] ForwardB
);

  wire comparator_2_eq, comparator_4_eq, eqAm, eqAw, eqBm, eqBw, nexA, nexB, nzm, nzw, wA0, wB0;

  Comparator #(.width(5)) comparator_1 (.a(rd_w), .b(rs1_e), .eq(eqAw));  // open: gt, lt
  and and_1 (ForwardA[1], RegWrite_m, nzm, eqAm);
  not not_1 (nexA, ForwardA[1]);
  and and_2 (ForwardA[0], wA0, nexA);
  Comparator #(.width(5)) comparator_2 (.a(rd_m), .b({5{1'b0}}), .eq(comparator_2_eq));  // open: gt, lt
  Comparator #(.width(5)) comparator_3 (.a(rd_m), .b(rs1_e), .eq(eqAm));  // open: gt, lt
  not not_2 (nzm, comparator_2_eq);
  and and_3 (wA0, RegWrite_w, nzw, eqAw);
  Comparator #(.width(5)) comparator_4 (.a(rd_w), .b({5{1'b0}}), .eq(comparator_4_eq));  // open: gt, lt
  Comparator #(.width(5)) comparator_5 (.a(rd_w), .b(rs2_e), .eq(eqBw));  // open: gt, lt
  not not_3 (nzw, comparator_4_eq);
  and and_4 (ForwardB[1], RegWrite_m, nzm, eqBm);
  not not_4 (nexB, ForwardB[1]);
  and and_5 (ForwardB[0], wB0, nexB);
  Comparator #(.width(5)) comparator_6 (.a(rd_m), .b(rs2_e), .eq(eqBm));  // open: gt, lt
  and and_6 (wB0, RegWrite_w, nzw, eqBw);

  // Other names for the same wires on the sheet: wA = ForwardA[0]; exA = ForwardA[1]; wB = ForwardB[0];
  //   exB = ForwardB[1]
endmodule

module WBBypass (
  input  [4:0] rs1,
  input  [4:0] rs2,
  input  [4:0] rd_w,
  input  RegWrite_w,
  input  [31:0] WD,
  input  [31:0] RF1,
  input  [31:0] RF2,
  output [31:0] RD1,
  output [31:0] RD2
);

  wire comparator_1_eq, e1, e2, h1, h2, nz;

  not not_1 (nz, comparator_1_eq);
  Comparator #(.width(5)) comparator_1 (.a(rd_w), .b({5{1'b0}}), .eq(comparator_1_eq));  // open: gt, lt
  Comparator #(.width(5)) comparator_2 (.a(rd_w), .b(rs1), .eq(e1));  // open: gt, lt
  and and_1 (h1, RegWrite_w, nz, e1);
  Multiplexer #(.width(32)) multiplexer_1 (.in0(RF1), .in1(WD), .out(RD1), .sel(h1));
  Comparator #(.width(5)) comparator_3 (.a(rd_w), .b(rs2), .eq(e2));  // open: gt, lt
  and and_2 (h2, RegWrite_w, nz, e2);
  Multiplexer #(.width(32)) multiplexer_2 (.in0(RF2), .in1(WD), .out(RD2), .sel(h2));
endmodule

module HazardUnit (
  input  MemRead_e,
  input  [4:0] rd_e,
  input  [4:0] rs1_d,
  input  [4:0] rs2_d,
  output Stall
);

  wire any, comparator_1_eq, e1, e2, nz;

  not not_1 (nz, comparator_1_eq);
  Comparator #(.width(5)) comparator_1 (.a(rd_e), .b({5{1'b0}}), .eq(comparator_1_eq));  // open: gt, lt
  Comparator #(.width(5)) comparator_2 (.a(rd_e), .b(rs1_d), .eq(e1));  // open: gt, lt
  Comparator #(.width(5)) comparator_3 (.a(rd_e), .b(rs2_d), .eq(e2));  // open: gt, lt
  or or_1 (any, e1, e2);
  and and_1 (Stall, MemRead_e, nz, any);
endmodule

module LoadExt (
  input  [31:0] Word,
  input  [1:0] A,
  input  [2:0] funct3,
  output [31:0] Y
);

  wire [31:0] lbs, lbu, lhs, lhu, v;

  Shifter #(.shift("lr"), .width(32)) shifter_1 (.in(Word), .\dist ({A, 3'b000}), .out(v));
  assign lbs = {{24{v[7]}}, v[7:0]};  // Bit_Extender bit_extender_1
  assign lbu = {{24{1'b0}}, v[7:0]};  // Bit_Extender bit_extender_2
  assign lhs = {{16{v[15]}}, v[15:0]};  // Bit_Extender bit_extender_3
  assign lhu = {{16{1'b0}}, v[15:0]};  // Bit_Extender bit_extender_4
  Multiplexer #(.select(3), .width(32)) multiplexer_1 (
    .in0(lbs), .in1(lhs), .in2(v), .in3(v), .in4(lbu), .in5(lhu), .in6(v), .in7(v), .out(Y), .sel(funct3));
endmodule

module StoreMerge (
  input  [1:0] A,
  input  [31:0] Old,
  input  [31:0] WData,
  input  [2:0] funct3,
  output [31:0] Merged
);

  wire [1:0] k;
  wire [31:0] d, db, dh, ds, keep, km, ks, nks;

  Bit_Extender #(.in_width(3), .out_width(2)) bit_extender_1 (.in(funct3), .out(k));
  assign db = {{24{1'b0}}, WData[7:0]};  // Bit_Extender bit_extender_2
  assign dh = {{16{1'b0}}, WData[15:0]};  // Bit_Extender bit_extender_3
  Multiplexer #(.select(2), .width(32)) multiplexer_1 (.in0(db), .in1(dh), .in2(WData), .in3(WData), .out(d), .sel(k));
  Multiplexer #(.select(2), .width(32)) multiplexer_2 (
    .in0(32'hff), .in1(32'hffff), .in2({32{1'b1}}), .in3({32{1'b1}}), .out(km), .sel(k));
  Shifter #(.width(32)) shifter_1 (.in(d), .\dist ({A, 3'b000}), .out(ds));
  Shifter #(.width(32)) shifter_2 (.in(km), .\dist ({A, 3'b000}), .out(ks));
  assign nks = ~ks;  // NOT_Gate not_1, 32 bits wide
  assign keep = nks & Old;  // AND_Gate and_1, 32 bits wide
  assign Merged = ds | keep;  // OR_Gate or_1, 32 bits wide

  // Other names for the same wires on the sheet: sh[4:3] = A
endmodule

module MulDiv (
  input  [31:0] A,
  input  [31:0] B,
  input  [2:0] funct3,
  output [31:0] Y
);

  wire bz;
  wire [31:0] corr, dv, dvu, mul, mulh, mulhsu, mulhu, qs, qu, rm, rmu, rs, ru, sa;
  wire [32:0] a33, b33, qu33, ru33;

  assign corr = B & sa;  // AND_Gate and_1, 32 bits wide
  Shifter #(.shift("ar"), .width(32)) shifter_1 (.in(A), .\dist ({5{1'b1}}), .out(sa));
  Multiplier #(.mode("twosComplement"), .width(32)) multiplier_1 (
    .a(A), .b(B), .out(mul), .cin({32{1'b0}}), .cout(mulh));
  Multiplier #(.width(32)) multiplier_2 (.a(A), .b(B), .cin({32{1'b0}}), .cout(mulhu));  // open: out
  Subtractor #(.width(32)) subtractor_1 (.a(mulhu), .b(corr), .out(mulhsu));  // open: bin, bout
  Divider #(.mode("twosComplement"), .width(32)) divider_1 (.a(A), .b(B), .out(qs), .upper(sa), .rem(rs));
  assign a33 = {{1{1'b0}}, A};  // Bit_Extender bit_extender_1
  assign b33 = {{1{1'b0}}, B};  // Bit_Extender bit_extender_2
  Comparator #(.mode("unsigned"), .width(32)) comparator_1 (.a(B), .b({32{1'b0}}), .eq(bz));  // open: gt, lt
  Multiplexer #(.width(32)) multiplexer_1 (.in0(qs), .in1({32{1'b1}}), .out(dv), .sel(bz));
  Multiplexer #(.width(32)) multiplexer_2 (.in0(qu), .in1({32{1'b1}}), .out(dvu), .sel(bz));
  Multiplexer #(.width(32)) multiplexer_3 (.in0(rs), .in1(A), .out(rm), .sel(bz));
  Multiplexer #(.width(32)) multiplexer_4 (.in0(ru), .in1(A), .out(rmu), .sel(bz));
  Divider #(.width(33)) divider_2 (.a(a33), .b(b33), .out(qu33), .upper({33{1'b0}}), .rem(ru33));
  Bit_Extender #(.in_width(33), .out_width(32)) bit_extender_3 (.in(qu33), .out(qu));
  Bit_Extender #(.in_width(33), .out_width(32)) bit_extender_4 (.in(ru33), .out(ru));
  Multiplexer #(.select(3), .width(32)) multiplexer_5 (
    .in0(mul), .in1(mulh), .in2(mulhsu), .in3(mulhu), .in4(dv), .in5(dvu), .in6(rm), .in7(rmu), .out(Y),
    .sel(funct3));
endmodule

module IsMul (
  input  [31:0] Instr,
  output IsM
);

  wire b25, isr;
  wire [6:0] op;
  wire [31:0] s25;

  Bit_Extender #(.in_width(32), .out_width(7)) bit_extender_1 (.in(Instr), .out(op));
  Comparator #(.mode("unsigned"), .width(7)) comparator_1 (.a(op), .b(7'b0110011), .eq(isr));  // open: gt, lt
  Shifter #(.shift("lr"), .width(32)) shifter_1 (.in(Instr), .\dist (5'b11001), .out(s25));
  Bit_Extender #(.in_width(32), .out_width(1)) bit_extender_2 (.in(s25), .out(b25));
  and and_1 (IsM, isr, b25);
endmodule

module MemMap (
  input  [31:0] Addr,
  input  MemWrite,
  input  [31:0] MemRData,
  input  [31:0] IORData,
  output [31:0] RData,
  output RamWE,
  output IOWrite
);

  wire io, ram;

  Comparator #(.mode("unsigned"), .width(32)) comparator_1 (.a(Addr), .b(32'h80000000), .lt(ram));  // open: gt, eq
  not not_1 (io, ram);
  and and_1 (RamWE, MemWrite, ram);
  and and_2 (IOWrite, MemWrite, io);
  Multiplexer #(.width(32)) multiplexer_1 (.in0(MemRData), .in1(IORData), .out(RData), .sel(io));
endmodule

module BTB (
  input  [31:0] PC_f,
  input  [31:0] PC_e,
  input  [31:0] Target_e,
  input  Update,
  input  Taken,
  input  clk,
  input  Reset,
  output Pred,
  output [31:0] PTarget
);

  wire hit_e, hit_f, hot, we;
  wire [1:0] ctr_e, ctr_f, ctrnext, newctr;
  wire [4:0] idx_e, idx_f, lo_e, lo_f;
  wire [31:0] ctr32, key_e, key_f, newtgt, sh_e, sh_f, tag_e, tag_f, tgm, tgt_e, tgt_f;

  Shifter #(.shift("lr"), .width(32)) shifter_1 (.in(PC_f), .\dist (5'b00010), .out(sh_f));
  Bit_Extender #(.in_width(32), .out_width(5)) bit_extender_1 (.in(sh_f), .out(lo_f));
  assign idx_f = lo_f | 5'b10000;  // OR_Gate or_1, 5 bits wide
  assign key_f = PC_f | 32'h1;  // OR_Gate or_2, 32 bits wide
  Shifter #(.shift("lr"), .width(32)) shifter_2 (.in(PC_e), .\dist (5'b00010), .out(sh_e));
  Bit_Extender #(.in_width(32), .out_width(5)) bit_extender_2 (.in(sh_e), .out(lo_e));
  assign idx_e = lo_e | 5'b10000;  // OR_Gate or_3, 5 bits wide
  assign key_e = PC_e | 32'h1;  // OR_Gate or_4, 32 bits wide
  RegFile TAGS (
    .rs1(idx_f), .rs2(idx_e), .rd(idx_e), .WD(key_e), .RegWrite(we), .clk(clk), .Reset(Reset), .RD1(tag_f),
    .RD2(tag_e));
  RegFile TGTS (
    .rs1(idx_f), .rs2(idx_e), .rd(idx_e), .WD(newtgt), .RegWrite(we), .clk(clk), .Reset(Reset), .RD1(tgt_f),
    .RD2(tgt_e));
  Comparator #(.mode("unsigned"), .width(32)) comparator_1 (.a(tag_f), .b(key_f), .eq(hit_f));  // open: gt, lt
  Bit_Extender #(.in_width(32), .out_width(2)) bit_extender_3 (.in(tgt_f), .out(ctr_f));
  and and_1 (Pred, hit_f, ctr_f[1]);
  assign PTarget = tgt_f & 32'hfffffffc;  // AND_Gate and_2, 32 bits wide
  ROM #(.addrWidth(3), .dataWidth(2)) rom_1 (.addr({Taken, ctr_e}), .data(ctrnext));
  Comparator #(.mode("unsigned"), .width(32)) comparator_2 (.a(tag_e), .b(key_e), .eq(hit_e));  // open: gt, lt
  Bit_Extender #(.in_width(32), .out_width(2)) bit_extender_4 (.in(tgt_e), .out(ctr_e));
  Multiplexer #(.width(2)) multiplexer_1 (.in0(2'b10), .in1(ctrnext), .out(newctr), .sel(hit_e));
  assign ctr32 = {{30{1'b0}}, newctr};  // Bit_Extender bit_extender_5
  assign tgm = Target_e & 32'hfffffffc;  // AND_Gate and_3, 32 bits wide
  assign newtgt = tgm | ctr32;  // OR_Gate or_5, 32 bits wide
  or or_6 (hot, hit_e, Taken);
  and and_4 (we, Update, hot);

  // Other names for the same wires on the sheet: ctrhi_f = ctr_f[1]; raddr[2:0] = {Taken, ctr_e}

  // Notes on the sheet:
  //   contents of rom_1 (hex, n*v repeats v):
  //   0 0 1 2 1 2 3 3
endmodule

module PredRegs (
  input  Pred_f,
  input  EN,
  input  FlushD,
  input  FlushE,
  input  clk,
  input  Reset,
  output Pred_d,
  output Pred_e
);

  wire dd, de, ldd, nfd, nfe;

  Register #(.width(1)) register_1 (.D(dd), .en(ldd), .clk(clk), .Q(Pred_d), .clr(Reset));
  not not_1 (nfd, FlushD);
  and and_1 (dd, Pred_f, nfd);
  or or_1 (ldd, EN, FlushD);
  not not_2 (nfe, FlushE);
  Register #(.width(1)) register_2 (.D(de), .clk(clk), .Q(Pred_e), .clr(Reset));  // open: en
  and and_2 (de, Pred_d, nfe);

  // Other names for the same wires on the sheet: pd = Pred_d; pe = Pred_e
endmodule
