// Logisim project riscv_pipe.circ as structural Verilog: 5 circuits, main circuit main
module IMEM (
  input  [31:0] PC,
  output [31:0] Instr
);

  ROM #(.addrWidth(10), .dataWidth(32)) IROM (.addr(PC[11:2]), .data(Instr));

  // Notes on the sheet:
  //   contents of IROM (hex, n*v repeats v):
  //   500093 2081b3 40208233 80a283 50a623 208a63 10000ef 409393 40115413 123454b7 13
endmodule

module DMEM (
  input  [31:0] Addr,
  input  MemWrite,
  input  clk,
  input  [31:0] WData,
  input  [2:0] funct3,
  output [31:0] RData
);

  wire [1:0] a2;
  wire [31:0] din, dout;

  Bit_Extender #(.in_width(32), .out_width(2)) bit_extender_1 (.in(Addr), .out(a2));
  LoadExt loadext_1 (.Word(dout), .A(a2), .funct3(funct3), .Y(RData));
  StoreMerge storemerge_1 (.A(a2), .Old(dout), .WData(WData), .funct3(funct3), .Merged(din));
  RAM #(.addrWidth(10), .asyncread("true"), .dataWidth(32)) DRAM (
    .addr(Addr[11:2]), .we(MemWrite), .oe(1'b1), .clk(clk), .din(din), .dout(dout));

  // Other names for the same wires on the sheet: f3[2:0] = funct3
endmodule

module main (
);

  wire clk, cpu_1_iowrite, cpu_1_memwrite, cpu_1_regwrite, io_1_ttywe, rst;
  wire [4:0] cpu_1_rd;
  wire [6:0] io_1_ttydata;
  wire [7:0] dipswitch_1_sw8, io_1_led;
  wire [31:0] cpu_1_instr, cpu_1_instr_d, cpu_1_instr_e, cpu_1_instr_m, cpu_1_instr_w, cpu_1_memaddr,
       cpu_1_memwdata, cpu_1_pc, cpu_1_wb, io_1_hex, io_1_rdata;

  Clock clock_1 (.out(clk));
  Button RESET (.out(rst));
  // Probe on cpu_1_instr_w
  // Probe on cpu_1_instr_m
  // Probe on cpu_1_instr_e
  // Probe on cpu_1_instr_d
  // Probe on cpu_1_instr
  // Probe on cpu_1_pc
  // Probe on cpu_1_memwdata
  // Probe on cpu_1_memaddr
  // Probe on cpu_1_memwrite
  // Probe on cpu_1_wb
  // Probe on cpu_1_rd
  // Probe on cpu_1_regwrite
  CPU cpu_1 (
    .clk(clk), .Reset(rst), .IORData(io_1_rdata), .RegWrite(cpu_1_regwrite), .rd(cpu_1_rd), .WB(cpu_1_wb),
    .MemWrite(cpu_1_memwrite), .MemAddr(cpu_1_memaddr), .MemWData(cpu_1_memwdata), .PC(cpu_1_pc),
    .Instr(cpu_1_instr), .Instr_D(cpu_1_instr_d), .Instr_E(cpu_1_instr_e), .Instr_M(cpu_1_instr_m),
    .Instr_W(cpu_1_instr_w), .IOWrite(cpu_1_iowrite));
  IO io_1 (
    .Addr(cpu_1_memaddr), .WData(cpu_1_memwdata), .IOWrite(cpu_1_iowrite), .SW(dipswitch_1_sw8), .clk(clk),
    .HEX(io_1_hex), .RData(io_1_rdata), .LED(io_1_led), .TTYData(io_1_ttydata), .TTYWE(io_1_ttywe));
  Hex_Digit_Display hex_digit_display_1 (.value(io_1_hex[31:28]));  // open: dp
  Hex_Digit_Display hex_digit_display_2 (.value(io_1_hex[27:24]));  // open: dp
  TTY tty_1 (.data(io_1_ttydata), .clk(clk), .we(io_1_ttywe), .clr(rst));
  Hex_Digit_Display hex_digit_display_3 (.value(io_1_hex[23:20]));  // open: dp
  Hex_Digit_Display hex_digit_display_4 (.value(io_1_hex[19:16]));  // open: dp
  LedBar ledbar_1 (
    .led0(io_1_led[7]), .led1(io_1_led[6]), .led2(io_1_led[5]), .led3(io_1_led[4]), .led4(io_1_led[3]),
    .led5(io_1_led[2]), .led6(io_1_led[1]), .led7(io_1_led[0]));
  DipSwitch dipswitch_1 (
    .sw1(dipswitch_1_sw8[7]), .sw2(dipswitch_1_sw8[6]), .sw3(dipswitch_1_sw8[5]), .sw4(dipswitch_1_sw8[4]),
    .sw5(dipswitch_1_sw8[3]), .sw6(dipswitch_1_sw8[2]), .sw7(dipswitch_1_sw8[1]), .sw8(dipswitch_1_sw8[0]));
  Hex_Digit_Display hex_digit_display_5 (.value(io_1_hex[15:12]));  // open: dp
  Hex_Digit_Display hex_digit_display_6 (.value(io_1_hex[11:8]));  // open: dp
  Hex_Digit_Display hex_digit_display_7 (.value(io_1_hex[7:4]));  // open: dp
  Hex_Digit_Display hex_digit_display_8 (.value(io_1_hex[3:0]));  // open: dp
endmodule

module CPU (
  input  clk,
  input  Reset,
  input  [31:0] IORData,
  output RegWrite,
  output [4:0] rd,
  output [31:0] WB,
  output MemWrite,
  output [31:0] MemAddr,
  output [31:0] MemWData,
  output [31:0] PC,
  output [31:0] Instr,
  output [31:0] Instr_D,
  output [31:0] Instr_E,
  output [31:0] Instr_M,
  output [31:0] Instr_W,
  output IOWrite
);

  wire alusrc_d, alusrc_e, branch_d, branch_e, bt_e, idex_flush, ifid_en, ifid_flush, ism_e, jalr_d, jalr_e,
       jump_d, jump_e, memread_d, memread_e, memread_m, memwrite_d, memwrite_e, mis_e, mn_e, mt_e, npred_e,
       nselbr_e, pred_d, pred_e, pred_f, ramwe_m, regwrite_d, regwrite_e, regwrite_m, selbr_e, Stall,
       taken_e, upd_e;
  wire [1:0] fwda, fwdb, m2r_d, m2r_e, m2r_m, m2r_w;
  wire [2:0] f3_e, immsel_d;
  wire [3:0] aluctl_d, aluctl_e;
  wire [4:0] rd_e, rd_m, rs1_e, rs2_e;
  wire [31:0] alub_e, aluout_e, aluy_e, brt_e, dmrd_m, fa_e, fb_e, imm_d, imm_e, jalrt_e, mdy_e, pc1, pc1a,
       pc4_d, pc4_e, pc4_f, pc_d, pc_e, pc_m, pc_w, pcnext, ptgt_f, rd1_d, rd1_e, rd2_d, rd2_e, rdata_m,
       rdata_w, result_e, result_w, rf1_d, rf2_d, seq_f;

  PCUnit pcunit_1 (.PCnext(pcnext), .EN(ifid_en), .clk(clk), .Reset(Reset), .PC(PC), .PC4(pc4_f));
  IMEM imem_1 (.PC(PC), .Instr(Instr));
  IF_ID if_id_1 (
    .EN(ifid_en), .PC_in(PC), .Flush(ifid_flush), .clk(clk), .Reset(Reset), .PC4_in(pc4_f), .Instr_in(Instr),
    .PC_out(pc_d), .PC4_out(pc4_d), .Instr_out(Instr_D));
  ImmGen immgen_1 (.Instr(Instr_D), .ImmSel(immsel_d), .Imm(imm_d));
  RegFile regfile_1 (
    .rs1(Instr_D[19:15]), .rs2(Instr_D[24:20]), .rd(rd), .WD(WB), .RegWrite(RegWrite), .clk(clk),
    .Reset(Reset), .RD1(rf1_d), .RD2(rf2_d));
  Control control_1 (
    .Instr(Instr_D), .ALUctl(aluctl_d), .MemToReg(m2r_d), .MemWrite(memwrite_d), .MemRead(memread_d),
    .ALUSrc(alusrc_d), .RegWrite(regwrite_d), .Branch(branch_d), .Jump(jump_d), .Jalr(jalr_d),
    .ImmSel(immsel_d));
  WBBypass wbbypass_1 (
    .rs1(Instr_D[19:15]), .rs2(Instr_D[24:20]), .rd_w(rd), .RegWrite_w(RegWrite), .WD(WB), .RF1(rf1_d),
    .RF2(rf2_d), .RD1(rd1_d), .RD2(rd2_d));
  not not_1 (ifid_en, Stall);
  or or_1 (idex_flush, Stall, ifid_flush);
  ID_EX id_ex_1 (
    .PC_in(pc_d), .EN(1'b1), .Flush(idex_flush), .clk(clk), .PC4_in(pc4_d), .Reset(Reset), .RD1_in(rd1_d),
    .RegWrite_in(regwrite_d), .ALUSrc_in(alusrc_d), .RD2_in(rd2_d), .MemRead_in(memread_d),
    .MemWrite_in(memwrite_d), .MemToReg_in(m2r_d), .Imm_in(imm_d), .Branch_in(branch_d), .Jump_in(jump_d),
    .Jalr_in(jalr_d), .rs1_in(Instr_D[19:15]), .ALUctl_in(aluctl_d), .rs2_in(Instr_D[24:20]),
    .rd_in(Instr_D[11:7]), .f3_in(Instr_D[14:12]), .Instr_in(Instr_D), .PC_out(pc_e), .PC4_out(pc4_e),
    .RD1_out(rd1_e), .RegWrite_out(regwrite_e), .ALUSrc_out(alusrc_e), .RD2_out(rd2_e),
    .MemRead_out(memread_e), .MemWrite_out(memwrite_e), .MemToReg_out(m2r_e), .Imm_out(imm_e),
    .Branch_out(branch_e), .Jump_out(jump_e), .Jalr_out(jalr_e), .rs1_out(rs1_e), .ALUctl_out(aluctl_e),
    .rs2_out(rs2_e), .rd_out(rd_e), .f3_out(f3_e), .Instr_out(Instr_E));
  HazardUnit hazardunit_1 (
    .MemRead_e(memread_e), .rd_e(rd_e), .rs1_d(Instr_D[19:15]), .rs2_d(Instr_D[24:20]), .Stall(Stall));
  Adder #(.width(32)) adder_1 (.a(pc_e), .b(imm_e), .out(brt_e));  // open: cin, cout
  and and_1 (bt_e, branch_e, taken_e);
  or or_2 (selbr_e, bt_e, jump_e);
  Multiplexer #(.width(32)) multiplexer_1 (.in0(seq_f), .in1(brt_e), .out(pc1a), .sel(mt_e));
  assign jalrt_e = aluout_e & 32'hfffffffe;  // AND_Gate and_2, 32 bits wide
  Multiplexer #(.width(32)) multiplexer_2 (.in0(pc1), .in1(jalrt_e), .out(pcnext), .sel(jalr_e));
  or or_3 (ifid_flush, mis_e, jalr_e);
  Multiplexer #(.width(32)) multiplexer_3 (.in0(pc1a), .in1(pc4_e), .out(pc1), .sel(mn_e));
  not not_2 (npred_e, pred_e);
  not not_3 (nselbr_e, selbr_e);
  and and_3 (mt_e, selbr_e, npred_e);
  and and_4 (mn_e, nselbr_e, pred_e);
  or or_4 (mis_e, mt_e, mn_e);
  or or_5 (upd_e, branch_e, jump_e);
  Multiplexer #(.width(32)) multiplexer_4 (.in0(pc4_f), .in1(ptgt_f), .out(seq_f), .sel(pred_f));
  BTB btb_1 (
    .PC_f(PC), .PC_e(pc_e), .Target_e(brt_e), .Update(upd_e), .Taken(selbr_e), .clk(clk), .Reset(Reset),
    .Pred(pred_f), .PTarget(ptgt_f));
  PredRegs predregs_1 (
    .Pred_f(pred_f), .EN(ifid_en), .FlushD(ifid_flush), .FlushE(idex_flush), .clk(clk), .Reset(Reset),
    .Pred_d(pred_d), .Pred_e(pred_e));
  ForwardUnit forwardunit_1 (
    .rs1_e(rs1_e), .rs2_e(rs2_e), .rd_m(rd_m), .RegWrite_m(regwrite_m), .rd_w(rd), .RegWrite_w(RegWrite),
    .ForwardA(fwda), .ForwardB(fwdb));
  Multiplexer #(.select(2), .width(32)) multiplexer_5 (
    .in0(rd1_e), .in1(WB), .in2(MemAddr), .in3(MemAddr), .out(fa_e), .sel(fwda));
  Multiplexer #(.select(2), .width(32)) multiplexer_6 (
    .in0(rd2_e), .in1(WB), .in2(MemAddr), .in3(MemAddr), .out(fb_e), .sel(fwdb));
  Multiplexer #(.select(2), .width(32)) multiplexer_7 (
    .in0(aluout_e), .in1(aluout_e), .in2(pc4_e), .in3(pc4_e), .out(result_e), .sel(m2r_e));
  Multiplexer #(.width(32)) multiplexer_8 (.in0(fb_e), .in1(imm_e), .out(alub_e), .sel(alusrc_e));
  Multiplexer #(.width(32)) multiplexer_9 (.in0(aluy_e), .in1(mdy_e), .out(aluout_e), .sel(ism_e));
  BranchCmp branchcmp_1 (.A(fa_e), .B(fb_e), .funct3(f3_e), .Taken(taken_e));  // open: Eq, Lt, Ltu
  ALU alu_1 (.A(fa_e), .B(alub_e), .ALUctl(aluctl_e), .Y(aluy_e));  // open: Zero
  MulDiv muldiv_1 (.A(fa_e), .B(fb_e), .funct3(f3_e), .Y(mdy_e));
  IsMul ismul_1 (.Instr(Instr_E), .IsM(ism_e));
  EX_MEM ex_mem_1 (
    .EN(1'b1), .PC_in(pc_e), .Flush(1'b0), .clk(clk), .Reset(Reset), .Result_in(result_e),
    .Instr_in(Instr_E), .WData_in(fb_e), .rd_in(rd_e), .RegWrite_in(regwrite_e), .MemToReg_in(m2r_e),
    .MemRead_in(memread_e), .MemWrite_in(memwrite_e), .PC_out(pc_m), .Result_out(MemAddr),
    .Instr_out(Instr_M), .WData_out(MemWData), .rd_out(rd_m), .RegWrite_out(regwrite_m),
    .MemToReg_out(m2r_m), .MemRead_out(memread_m), .MemWrite_out(MemWrite));
  DMEM dmem_1 (
    .Addr(MemAddr), .MemWrite(ramwe_m), .clk(clk), .WData(MemWData), .funct3(Instr_M[14:12]), .RData(dmrd_m));
  MemMap memmap_1 (
    .Addr(MemAddr), .MemWrite(MemWrite), .MemRData(dmrd_m), .IORData(IORData), .RData(rdata_m),
    .RamWE(ramwe_m), .IOWrite(IOWrite));
  MEM_WB mem_wb_1 (
    .EN(1'b1), .PC_in(pc_m), .Flush(1'b0), .clk(clk), .Reset(Reset), .Result_in(MemAddr), .Instr_in(Instr_M),
    .RData_in(rdata_m), .rd_in(rd_m), .RegWrite_in(regwrite_m), .MemToReg_in(m2r_m), .PC_out(pc_w),
    .Result_out(result_w), .Instr_out(Instr_W), .RData_out(rdata_w), .rd_out(rd), .RegWrite_out(RegWrite),
    .MemToReg_out(m2r_w));
  Multiplexer #(.select(2), .width(32)) multiplexer_10 (
    .in0(result_w), .in1(rdata_w), .in2(result_w), .in3(rdata_w), .out(WB), .sel(m2r_w));

  // Other names for the same wires on the sheet: rd_d[4:0] = Instr_D[11:7]; f3_d[2:0] = Instr_D[14:12];
  //   rs1_d[4:0] = Instr_D[19:15]; rs2_d[4:0] = Instr_D[24:20]; instr_f[31:0] = Instr; f3_m[2:0] = Instr_M[14:12];
  //   memwrite_m = MemWrite; pc_en = ifid_en; pc_f[31:0] = PC; pcsel_e = ifid_flush; rd_w[4:0] = rd;
  //   regwrite_w = RegWrite; result_m[31:0] = MemAddr; wb_w[31:0] = WB; wdata_m[31:0] = MemWData
endmodule

module IO (
  input  [31:0] Addr,
  input  [31:0] WData,
  input  IOWrite,
  input  [7:0] SW,
  input  clk,
  output [31:0] HEX,
  output [31:0] RData,
  output [7:0] LED,
  output [6:0] TTYData,
  output TTYWE
);

  wire d0, d1, d2, d3, wehex, weled;
  wire [1:0] sel;
  wire [31:0] a2, ledq, swz;

  Shifter #(.shift("lr"), .width(32)) shifter_1 (.in(Addr), .\dist (5'b00010), .out(a2));
  Bit_Extender #(.in_width(32), .out_width(2)) bit_extender_1 (.in(a2), .out(sel));
  Decoder #(.enable("false"), .select(2)) decoder_1 (.out0(d0), .out1(d1), .out2(d2), .out3(d3), .sel(sel));
  and and_1 (weled, IOWrite, d0);
  and and_2 (wehex, IOWrite, d1);
  and and_3 (TTYWE, IOWrite, d2);
  Register #(.width(32)) LEDREG (.D(WData), .en(weled), .clk(clk), .Q(ledq));  // open: clr
  Register #(.width(32)) register_1 (.D(WData), .en(wehex), .clk(clk), .Q(HEX));  // open: clr
  Bit_Extender #(.in_width(32), .out_width(8)) bit_extender_2 (.in(ledq), .out(LED));
  Bit_Extender #(.in_width(32), .out_width(7)) bit_extender_3 (.in(WData), .out(TTYData));
  assign swz = {{24{1'b0}}, SW};  // Bit_Extender bit_extender_4
  Multiplexer #(.select(2), .width(32)) multiplexer_1 (
    .in0(ledq), .in1(HEX), .in2(32'h1), .in3(swz), .out(RData), .sel(sel));
endmodule
