// Logisim project riscv_single.circ as structural Verilog: 5 circuits, main circuit main
module IMEM (
  input  [31:0] PC,
  output [31:0] Instr
);

  ROM #(.addrWidth(10), .dataWidth(32)) IROM (.addr(PC[11:2]), .data(Instr));

  // Notes on the sheet:
  //   contents of IROM (hex, n*v repeats v):
  //   80000437 40413 6c6c62b7 54828293 20502023 6f7722b7 6f28293 20502223 a6472b7 c7228293 20502423
  //   20002623 20000393 3c303 30863 642423 138393 ff1ff06f c42283 542023 148493 942223 ff1ff06f
endmodule

module DMEM (
  input  [31:0] Addr,
  input  MemWrite,
  input  clk,
  input  [31:0] WData,
  input  [2:0] funct3,
  output [31:0] RData
);

  wire [1:0] a2;
  wire [31:0] din, dout;

  Bit_Extender #(.in_width(32), .out_width(2)) bit_extender_1 (.in(Addr), .out(a2));
  LoadExt loadext_1 (.Word(dout), .A(a2), .funct3(funct3), .Y(RData));
  StoreMerge storemerge_1 (.A(a2), .Old(dout), .WData(WData), .funct3(funct3), .Merged(din));
  RAM #(.addrWidth(10), .asyncread("true"), .dataWidth(32)) DRAM (
    .addr(Addr[11:2]), .we(MemWrite), .oe(1'b1), .clk(clk), .din(din), .dout(dout));

  // Other names for the same wires on the sheet: f3[2:0] = funct3
endmodule

module main (
);

  wire clk, cpu_1_iowrite, cpu_1_memwrite, cpu_1_regwrite, io_1_ttywe, rst;
  wire [4:0] cpu_1_rd;
  wire [6:0] io_1_ttydata;
  wire [7:0] dipswitch_1_sw8, io_1_led;
  wire [31:0] cpu_1_instr, cpu_1_memaddr, cpu_1_memwdata, cpu_1_pc, cpu_1_wb, io_1_hex, io_1_rdata;

  Button RESET (.out(rst));
  Clock clock_1 (.out(clk));
  // Probe on cpu_1_instr
  // Probe on cpu_1_pc
  // Probe on cpu_1_memwdata
  // Probe on cpu_1_memaddr
  // Probe on cpu_1_memwrite
  // Probe on cpu_1_wb
  // Probe on cpu_1_rd
  // Probe on cpu_1_regwrite
  CPU cpu_1 (
    .clk(clk), .Reset(rst), .IORData(io_1_rdata), .RegWrite(cpu_1_regwrite), .rd(cpu_1_rd), .WB(cpu_1_wb),
    .MemWrite(cpu_1_memwrite), .MemAddr(cpu_1_memaddr), .MemWData(cpu_1_memwdata), .PC(cpu_1_pc),
    .Instr(cpu_1_instr), .IOWrite(cpu_1_iowrite));
  IO io_1 (
    .Addr(cpu_1_memaddr), .WData(cpu_1_memwdata), .IOWrite(cpu_1_iowrite), .SW(dipswitch_1_sw8), .clk(clk),
    .HEX(io_1_hex), .RData(io_1_rdata), .LED(io_1_led), .TTYData(io_1_ttydata), .TTYWE(io_1_ttywe));
  Hex_Digit_Display hex_digit_display_1 (.value(io_1_hex[31:28]));  // open: dp
  Hex_Digit_Display hex_digit_display_2 (.value(io_1_hex[27:24]));  // open: dp
  Hex_Digit_Display hex_digit_display_3 (.value(io_1_hex[23:20]));  // open: dp
  TTY tty_1 (.data(io_1_ttydata), .clk(clk), .we(io_1_ttywe), .clr(rst));
  Hex_Digit_Display hex_digit_display_4 (.value(io_1_hex[19:16]));  // open: dp
  Hex_Digit_Display hex_digit_display_5 (.value(io_1_hex[15:12]));  // open: dp
  LedBar ledbar_1 (
    .led0(io_1_led[7]), .led1(io_1_led[6]), .led2(io_1_led[5]), .led3(io_1_led[4]), .led4(io_1_led[3]),
    .led5(io_1_led[2]), .led6(io_1_led[1]), .led7(io_1_led[0]));
  DipSwitch dipswitch_1 (
    .sw1(dipswitch_1_sw8[7]), .sw2(dipswitch_1_sw8[6]), .sw3(dipswitch_1_sw8[5]), .sw4(dipswitch_1_sw8[4]),
    .sw5(dipswitch_1_sw8[3]), .sw6(dipswitch_1_sw8[2]), .sw7(dipswitch_1_sw8[1]), .sw8(dipswitch_1_sw8[0]));
  Hex_Digit_Display hex_digit_display_6 (.value(io_1_hex[11:8]));  // open: dp
  Hex_Digit_Display hex_digit_display_7 (.value(io_1_hex[7:4]));  // open: dp
  Hex_Digit_Display hex_digit_display_8 (.value(io_1_hex[3:0]));  // open: dp
endmodule

module CPU (
  input  clk,
  input  Reset,
  input  [31:0] IORData,
  output RegWrite,
  output [4:0] rd,
  output [31:0] WB,
  output MemWrite,
  output [31:0] MemAddr,
  output [31:0] MemWData,
  output [31:0] PC,
  output [31:0] Instr,
  output IOWrite
);

  wire alusrc, branch, bt, ism, jalr, jump, ramwe, selbr, taken;
  wire [1:0] m2r;
  wire [2:0] immsel;
  wire [3:0] aluctl;
  wire [31:0] alub, aluy, brt, dmrd, imm, jalrt, mdy, pc1, pc4, pcnext, rd1, rdata;

  Multiplexer #(.select(2), .width(32)) multiplexer_1 (
    .in0(MemAddr), .in1(rdata), .in2(pc4), .in3({32{1'b0}}), .out(WB), .sel(m2r));
  MemMap memmap_1 (
    .Addr(MemAddr), .MemWrite(MemWrite), .MemRData(dmrd), .IORData(IORData), .RData(rdata), .RamWE(ramwe),
    .IOWrite(IOWrite));
  DMEM dmem_1 (.Addr(MemAddr), .MemWrite(ramwe), .clk(clk), .WData(MemWData), .funct3(Instr[14:12]), .RData(dmrd));
  BranchCmp branchcmp_1 (.A(rd1), .B(MemWData), .funct3(Instr[14:12]), .Taken(taken));  // open: Eq, Lt, Ltu
  Adder #(.width(32)) adder_1 (.a(PC), .b(imm), .out(brt));  // open: cin, cout
  Multiplexer #(.width(32)) multiplexer_2 (.in0(pc4), .in1(brt), .out(pc1), .sel(selbr));
  Multiplexer #(.width(32)) multiplexer_3 (.in0(pc1), .in1(jalrt), .out(pcnext), .sel(jalr));
  Multiplexer #(.width(32)) multiplexer_4 (.in0(MemWData), .in1(imm), .out(alub), .sel(alusrc));
  and and_1 (bt, branch, taken);
  or or_1 (selbr, bt, jump);
  assign jalrt = MemAddr & 32'hfffffffe;  // AND_Gate and_2, 32 bits wide
  ALU alu_1 (.A(rd1), .B(alub), .ALUctl(aluctl), .Y(aluy));  // open: Zero
  RegFile regfile_1 (
    .rs1(Instr[19:15]), .rs2(Instr[24:20]), .rd(Instr[11:7]), .WD(WB), .RegWrite(RegWrite), .clk(clk),
    .Reset(Reset), .RD1(rd1), .RD2(MemWData));
  ImmGen immgen_1 (.Instr(Instr), .ImmSel(immsel), .Imm(imm));
  IMEM imem_1 (.PC(PC), .Instr(Instr));
  PCUnit pcunit_1 (.PCnext(pcnext), .EN(1'b1), .clk(clk), .Reset(Reset), .PC(PC), .PC4(pc4));
  Control control_1 (
    .Instr(Instr), .ALUctl(aluctl), .MemToReg(m2r), .MemWrite(MemWrite), .ALUSrc(alusrc),
    .RegWrite(RegWrite), .Branch(branch), .Jump(jump), .Jalr(jalr), .ImmSel(immsel));  // open: MemRead
  Multiplexer #(.width(32)) multiplexer_5 (.in0(aluy), .in1(mdy), .out(MemAddr), .sel(ism));
  MulDiv muldiv_1 (.A(rd1), .B(MemWData), .funct3(Instr[14:12]), .Y(mdy));
  IsMul ismul_1 (.Instr(Instr), .IsM(ism));

  assign rd = Instr[11:7];

  // Other names for the same wires on the sheet: aluout[31:0] = MemAddr; f3[2:0] = Instr[14:12];
  //   rs1[4:0] = Instr[19:15]; rs2[4:0] = Instr[24:20]; rd2[31:0] = MemWData
endmodule

module IO (
  input  [31:0] Addr,
  input  [31:0] WData,
  input  IOWrite,
  input  [7:0] SW,
  input  clk,
  output [31:0] HEX,
  output [31:0] RData,
  output [7:0] LED,
  output [6:0] TTYData,
  output TTYWE
);

  wire d0, d1, d2, d3, wehex, weled;
  wire [1:0] sel;
  wire [31:0] a2, ledq, swz;

  Shifter #(.shift("lr"), .width(32)) shifter_1 (.in(Addr), .\dist (5'b00010), .out(a2));
  Bit_Extender #(.in_width(32), .out_width(2)) bit_extender_1 (.in(a2), .out(sel));
  Decoder #(.enable("false"), .select(2)) decoder_1 (.out0(d0), .out1(d1), .out2(d2), .out3(d3), .sel(sel));
  and and_1 (weled, IOWrite, d0);
  and and_2 (wehex, IOWrite, d1);
  and and_3 (TTYWE, IOWrite, d2);
  Register #(.width(32)) LEDREG (.D(WData), .en(weled), .clk(clk), .Q(ledq));  // open: clr
  Register #(.width(32)) register_1 (.D(WData), .en(wehex), .clk(clk), .Q(HEX));  // open: clr
  Bit_Extender #(.in_width(32), .out_width(8)) bit_extender_2 (.in(ledq), .out(LED));
  Bit_Extender #(.in_width(32), .out_width(7)) bit_extender_3 (.in(WData), .out(TTYData));
  assign swz = {{24{1'b0}}, SW};  // Bit_Extender bit_extender_4
  Multiplexer #(.select(2), .width(32)) multiplexer_1 (
    .in0(ledq), .in1(HEX), .in2(32'h1), .in3(swz), .out(RData), .sel(sel));
endmodule
